# Fritzing sketch alarm_pir (saved by Fritzing 0.9.2b)

parts:
  Raspberry_Pi1 = Raspberry Pi B+
  LED1 = RGB LED (com. cathode, rgb) [package="5 mm [THT]"]
  R1 = Resistor [tolerance=±5% resistance=220 package=THT]
  J1 = Infrared Proximity Sensor
  R3 = Resistor [tolerance=±5% resistance=220 package=THT]
  S1 = Pushbutton [package=THT]

nets:
  N1: Raspberry_Pi1.GPIO25, S1.leg0
  GND: Raspberry_Pi1.GND, LED1.common_cathode, J1.GND, S1.leg1
  N2: Raspberry_Pi1.GPIO23, R3.Pin_0
  N3: Raspberry_Pi1.GPIO15, R1.Pin_0
  N4: Raspberry_Pi1.GPIO14, J1.Vout
  5V: Raspberry_Pi1.5V, J1.Vcc
  N5: LED1.red_anode, R1.Pin_1
  N6: LED1.green_anode, R3.Pin_1
